// Logisim project exemplo_CLK.circ as structural Verilog: 4 circuits, main circuit main
module main (
);

  wire clk_out, dois_1_saida, quatro_1_saida, reset_out, um_1_saida;
  wire [7:0] dois_1_data, quatro_1_data, um_1_data;

  Clock clk (.out(clk_out));
  Button reset (.out(reset_out));
  // Probe on um_1_data
  // Probe on dois_1_data
  // Probe on quatro_1_data
  um um_1 (.clk(clk_out), .reset(reset_out), .saida(um_1_saida), .data(um_1_data));
  dois dois_1 (.reset(reset_out), .clk(clk_out), .saida(dois_1_saida), .data(dois_1_data));
  quatro quatro_1 (.reset(reset_out), .clk(clk_out), .saida(quatro_1_saida), .data(quatro_1_data));
  // Digital_Oscilloscope digital_oscilloscope_1: pin names not known; wires that end beside it: clk_out, um_1_saida, dois_1_saida, quatro_1_saida, reset_out
endmodule

module um (
  input  clk,
  input  reset,
  output saida,
  output [7:0] data
);

  Counter counter_1 (.Q(data), .clk(clk), .clr(reset));  // open: load, D, count, carry, up

  assign saida = clk;
endmodule

module quatro (
  input  reset,
  input  clk,
  output saida,
  output [7:0] data
);

  wire d_ff_1_q, d_ff_2_q, d_ff_3_q;

  D_Flip_Flop d_ff_1 (.D(saida), .clk(clk), .Q(d_ff_1_q), .preset(reset));  // open: Qn, reset
  D_Flip_Flop d_ff_2 (.D(d_ff_1_q), .clk(clk), .Q(d_ff_2_q), .reset(reset));  // open: Qn, preset
  D_Flip_Flop d_ff_3 (.D(d_ff_2_q), .clk(clk), .Q(d_ff_3_q), .reset(reset));  // open: Qn, preset
  D_Flip_Flop d_ff_4 (.D(d_ff_3_q), .clk(clk), .Q(saida), .reset(reset));  // open: Qn, preset
  Counter counter_1 (.Q(data), .clk(saida), .clr(reset));  // open: load, D, count, carry, up
endmodule

module dois (
  input  reset,
  input  clk,
  output saida,
  output [7:0] data
);

  wire d_ff_1_q;

  D_Flip_Flop d_ff_1 (.D(saida), .clk(clk), .Q(d_ff_1_q), .preset(reset));  // open: Qn, reset
  D_Flip_Flop d_ff_2 (.D(d_ff_1_q), .clk(clk), .Q(saida), .reset(reset));  // open: Qn, preset
  Counter counter_1 (.Q(data), .clk(saida), .clr(reset));  // open: load, D, count, carry, up
endmodule
